// Logisim project cpu.circ as structural Verilog: 2 circuits, main circuit main
module main (
  input  in_1,
  input  in_2,
  input  [15:0] in_3,
  input  [15:0] in_4,
  input  Reset,
  input  [15:0] From_Instr_Mem,
  input  clk,
  output [15:0] r0,
  output [15:0] r1,
  output [15:0] r2,
  output [15:0] r3,
  output [15:0] Display_0,
  output [15:0] Display_1,
  output [15:0] To_Instr_Mem,
  output [15:0] Data_Mem_Data,
  output [15:0] Data_Mem_Addr,
  output Data_Mem_Write
);

  wire not_1_out, overflow;
  wire [1:0] rd, rs, rt;
  wire [3:0] opcode;
  wire [5:0] funct;
  wire [7:0] offset_immediate;
  wire [11:0] target_addr;
  wire [15:0] InstIn, pc, R_Registers_read_data_1, R_Registers_read_data_2, ram_1_data;

  RAM #(.addrWidth(16), .dataWidth(16)) ram_1 (
    .addr(From_Instr_Mem), .data(ram_1_data), .sel(1'b1), .clk(clk), .ld(not_1_out), .clr(Reset));
  not not_1 (not_1_out, in_1);
  assign ram_1_data = in_1 ? InstIn : 16'bz;  // Controlled_Buffer controlled_buffer_1
  InstDecode Inst_Decode (
    .Inst(ram_1_data), .funct(funct), .rd(rd), .rt(rt), .rs(rs), .target_address(target_addr),
    .offset_immediate(offset_immediate), .opcode(opcode));
  Register #(.width(16)) u_PC (.Q(pc));  // open: D, en, clk, clr
  Regfile_main R_Registers (
    .Read_register_1(rs), .Read_register_2(rt), .write_register(rd), .Reg_0_Value(r0), .Reg_1_Value(r1),
    .Reg_2_Value(r2), .Reg_3_Value(r3), .clock(clk), .Read_Data_1(R_Registers_read_data_1),
    .Read_Data_2(R_Registers_read_data_2));  // open: write_data, RegWrite
  alu_main ALU (.Signed_Overflow(overflow));  // open: Switch__S, X, Equal, RESULT, Y
  Hex_Digit_Display hex_digit_display_1 (.value(Display_0[15:12]));  // open: dp
  Hex_Digit_Display hex_digit_display_2 (.value(Display_0[11:8]));  // open: dp
  Hex_Digit_Display hex_digit_display_3 (.value(Display_0[7:4]));  // open: dp
  Register #(.width(16)) register_1 (.D(in_3), .en(in_2), .Q(Display_0), .clk(clk));  // open: clr
  Register #(.width(16)) register_2 (.D(in_4), .en(in_2), .Q(Display_1), .clk(clk));  // open: clr
  Hex_Digit_Display hex_digit_display_4 (.value(Display_1[15:12]));  // open: dp
  Hex_Digit_Display hex_digit_display_5 (.value(Display_0[3:0]));  // open: dp
  Hex_Digit_Display hex_digit_display_6 (.value(Display_1[7:4]));  // open: dp
  Hex_Digit_Display hex_digit_display_7 (.value(Display_1[11:8]));  // open: dp
  LED led_1 (.in(overflow));
  Hex_Digit_Display hex_digit_display_8 (.value(Display_1[3:0]));  // open: dp

  // Other names for the same wires on the sheet: d0[15:0] = Display_0; d1[15:0] = Display_1; displayEnable = in_2;
  //   InstMemWrite = in_1; Instruction_Address[15:0] = From_Instr_Mem

  // Notes on the sheet:
  //   Instruction Memory
  //   This is the current PC that you need to send as OUTPUT
  //   This is the instruction that you would receive as INPUT
  //   This is a CLK that is an INPUT driven from the harness.
  //   Remember, this circuit is loaded from the harness to be tested!
  //   DO NOT CHANGE THE LOCATIONS OF THE INPUTS OR OUTPUTS! IF YOU DO SO, YOU NEED TO MAKE SURE THE PINS ARE IN THE RIGHT PLACES!
  //   These are OUTPUTS of the circuit
  //   These are OUTPUTS of the circuit
endmodule

module InstDecode (
  input  [15:0] Inst,
  output [5:0] funct,
  output [1:0] rd,
  output [1:0] rt,
  output [1:0] rs,
  output [11:0] target_address,
  output [7:0] offset_immediate,
  output [3:0] opcode
);

  wire [11:0] demultiplexer_1_out1, demultiplexer_1_out2, demultiplexer_1_out3, demultiplexer_1_out4,
       demultiplexer_1_out5, demultiplexer_1_out6, demultiplexer_1_out7, demultiplexer_1_out8,
       demultiplexer_1_out9, demultiplexer_1_out10, demultiplexer_1_out11, demultiplexer_1_out12;
  wire [11:8] demultiplexer_1_out0, multiplexer_1_out;

  Demultiplexer #(.select(4), .width(12)) demultiplexer_1 (
    .out0({demultiplexer_1_out0, rd, funct}), .out1(demultiplexer_1_out1), .out2(demultiplexer_1_out2),
    .out3(demultiplexer_1_out3), .out4(demultiplexer_1_out4), .out5(demultiplexer_1_out5),
    .out6(demultiplexer_1_out6), .out7(demultiplexer_1_out7), .out8(demultiplexer_1_out8),
    .out9(demultiplexer_1_out9), .out10(demultiplexer_1_out10), .out11(demultiplexer_1_out11),
    .out12(demultiplexer_1_out12), .in(Inst[11:0]), .sel(Inst[15:12]));  // open: out13, out14, out15, en
  Multiplexer #(.select(4), .width(12)) multiplexer_1 (
    .in0({12{1'b0}}), .in1({12{1'b0}}), .in2({12{1'b0}}), .in3({12{1'b0}}), .in4(demultiplexer_1_out4),
    .in5(demultiplexer_1_out5), .in6(demultiplexer_1_out6), .in7(demultiplexer_1_out7),
    .in8(demultiplexer_1_out8), .in9(demultiplexer_1_out9), .in10(demultiplexer_1_out10),
    .in11(demultiplexer_1_out11), .in12(demultiplexer_1_out12), .in13({12{1'b0}}), .in14({12{1'b0}}),
    .in15({12{1'b0}}), .out({multiplexer_1_out, offset_immediate}), .sel(Inst[15:12]));  // open: en
  assign rt = demultiplexer_1_out0[9:8] | multiplexer_1_out[9:8];  // OR_Gate or_1, 2 bits wide
  assign rs = demultiplexer_1_out0[11:10] | demultiplexer_1_out3[11:10] | multiplexer_1_out[11:10];  // OR_Gate or_2, 2 bits wide
  assign target_address = demultiplexer_1_out1 | demultiplexer_1_out2;  // OR_Gate or_3, 12 bits wide

  assign opcode = Inst[15:12];
endmodule
